# Fritzing sketch analogRead (saved by Fritzing 0.7.12b)
breadboards: 1

parts:
  Arduino1 = Arduino
  R1 = Photocell (LDR) [package=THT]
  R2 = 1.5k Ω Resistor [package=THT]
  R5 = Rotary Potentiometer (Small)

nets:
  N1: Arduino1.+5V, R1.pin_1, R5.leg1
  N2: Arduino1.GND, R2.Pin_0, R5.leg2
  N3: Arduino1.A0, R5.wiper
  N4: Arduino1.A5, R1.pin_0, R2.Pin_1
