# Fritzing sketch analogWrite (saved by Fritzing 0.7.12b)
breadboards: 3

parts:
  Arduino1 = Arduino
  SPKR1 = Loudspeaker
  Arduino2 = Arduino
  LED1 = green LED - 5mm
  R2 = 220 Ω Resistor [package=THT]
  R1 = 220 Ω Resistor [package=THT]
  Arduino4 = Arduino
  R3 = 220 Ω Resistor [package=THT]
  LED2 = green LED - 5mm
  R5 = Rotary Potentiometer (Small) [maximum_resistance=100kΩ]

nets:
  N1: Arduino1.GND, R1.Pin_0
  N2: Arduino1.D11, SPKR1.pin2
  N3: SPKR1.pin1, R1.Pin_1
  N4: Arduino2.GND, R2.Pin_0
  N5: Arduino2.D11, LED1.anode
  N6: LED1.cathode, R2.Pin_1
  N7: Arduino4.GND, R3.Pin_0, R5.leg1
  N8: Arduino4.D11, LED2.anode
  N9: Arduino4.+5V, R5.leg2
  N10: Arduino4.A0, R5.wiper
  N11: R3.Pin_1, LED2.cathode
